// Logisim project ULA IC.circ as structural Verilog: 3 circuits, main circuit Somador Completo
module Somador_Completo (
  input  A1,
  input  B1,
  input  A2,
  input  B2,
  output out_5,
  output out_6,
  output out_7,
  output out_8
);

  wire and_1_out, and_2_out, and_3_out, and_4_out, and_5_out, and_6_out, xor_1_out, xor_3_out;

  ExactlyOne xor_1 (.out(xor_1_out), .in0(A2), .in1(B2), .in2(out_5));
  and and_1 (and_1_out, out_5, A2);
  and and_2 (and_2_out, out_5, B2);
  and and_3 (and_3_out, B2, A2);
  xor xor_2 (out_7, xor_1_out, out_5);
  or or_1 (out_6, and_1_out, and_2_out, and_3_out);
  ExactlyOne xor_3 (.out(xor_3_out), .in0(A1), .in1(B1), .in2(1'b0));
  and and_4 (and_4_out, 1'b0, A1);
  and and_5 (and_5_out, 1'b0, B1);
  and and_6 (and_6_out, B1, A1);
  xor xor_4 (out_8, xor_3_out, 1'b0);
  or or_2 (out_5, and_4_out, and_5_out, and_6_out);
endmodule

module ALU_2Bits (
);

  Somador_Completo somador_completo ();  // open: A2, B2, out_5, A1, B1, out_6, out_7, out_8
  Subtrador_Completo subtrador_completo ();  // open: A1_2, B1_2, out_5, A1, B1, out_6, out_7, out_8
endmodule

module Subtrador_Completo (
  input  A1,
  input  B1,
  input  A1_2,
  input  B1_2,
  output out_5,
  output out_6,
  output out_7,
  output out_8
);

  wire and_1_out, and_2_out, and_3_out, and_4_out, and_5_out, and_6_out, not_1_out, not_2_out, not_3_out,
       not_4_out, xor_1_out, xor_3_out;

  not not_1 (not_1_out, A1_2);
  not not_2 (not_2_out, A1_2);
  xor xor_1 (xor_1_out, A1_2, B1_2);
  and and_1 (and_1_out, not_1_out, B1_2);
  and and_2 (and_2_out, not_2_out, out_5);
  and and_3 (and_3_out, B1_2, out_5);
  xor xor_2 (out_7, xor_1_out, out_5);
  or or_1 (out_6, and_1_out, and_2_out, and_3_out);
  not not_3 (not_3_out, A1);
  not not_4 (not_4_out, A1);
  xor xor_3 (xor_3_out, A1, B1);
  and and_4 (and_4_out, not_3_out, B1);
  and and_5 (and_5_out, not_4_out, 1'b0);
  and and_6 (and_6_out, B1, 1'b0);
  xor xor_4 (out_8, xor_3_out, 1'b0);
  or or_2 (out_5, and_4_out, and_5_out, and_6_out);
endmodule
