// Logisim project ULA2bits_grupo5.circ as structural Verilog: 7 circuits, main circuit Somador 2bits
// +
module Somador_2bits (
  input  A1,
  input  B1,
  input  A2,
  input  B2,
  output out_5,
  output out_6,
  output out_7
);

  wire and_1_out, and_2_out, and_3_out, and_4_out, and_5_out, and_6_out, or_2_out, xor_1_out, xor_3_out;

  xor xor_1 (xor_1_out, A2, B2);
  and and_1 (and_1_out, or_2_out, A2);
  and and_2 (and_2_out, or_2_out, B2);
  and and_3 (and_3_out, B2, A2);
  xor xor_2 (out_6, xor_1_out, or_2_out);
  or or_1 (out_5, and_1_out, and_2_out, and_3_out);
  ExactlyOne xor_3 (.out(xor_3_out), .in0(A1), .in1(B1), .in2(1'b0));
  and and_4 (and_4_out, 1'b0, A1);
  and and_5 (and_5_out, 1'b0, B1);
  and and_6 (and_6_out, B1, A1);
  xor xor_4 (out_7, xor_3_out, 1'b0);
  or or_2 (or_2_out, and_4_out, and_5_out, and_6_out);
endmodule

module ALU_2Bits (
  input  [1:0] A,
  input  [1:0] B,
  input  [1:0] in_3,
  output [4:0] out_4
);

  wire n7_seg_1_a_2, n7_seg_1_b_2, n7_seg_1_c_2, n7_seg_1_d_2, n7_seg_1_e, n7_seg_1_f, n7_seg_1_g;
  wire [2:0] somador_2bits_1_out_7;
  wire [3:0] multiplicador_2_bits_1_r4;
  wire [3:1] subtrador_2_bits_1_out_5;
  wire [4:0] divisor_2_bits_1_r1;

  Somador_2bits somador_2bits_1 (
    .A2(A[1]), .B2(B[1]), .A1(A[0]), .B1(B[0]), .out_5(somador_2bits_1_out_7[2]),
    .out_6(somador_2bits_1_out_7[1]), .out_7(somador_2bits_1_out_7[0]));
  Subtrador_2_bits subtrador_2_bits_1 (
    .A2(A[1]), .B2(B[1]), .A1(A[0]), .B1(B[0]), .out_5(subtrador_2_bits_1_out_5[1]),
    .out_6(subtrador_2_bits_1_out_5[2]), .out_7(subtrador_2_bits_1_out_5[3]));
  MUX_4x1 mux_4x1_1 (
    .Soma({2'b00, somador_2bits_1_out_7}), .Subtra({1'b0, subtrador_2_bits_1_out_5, 1'b0}),
    .Multipli({1'b0, multiplicador_2_bits_1_r4}), .Divisao(divisor_2_bits_1_r1), .BC1(in_3[1]),
    .BC2(in_3[0]), .out_7(out_4));
  Divisor_2_bits divisor_2_bits_1 (
    .A2(A[1]), .A1(A[0]), .B2(B[1]), .B1(B[0]), .E(divisor_2_bits_1_r1[4]), .Q1(divisor_2_bits_1_r1[2]),
    .Q0(divisor_2_bits_1_r1[3]), .R1(divisor_2_bits_1_r1[0]), .R0(divisor_2_bits_1_r1[1]));
  Multiplicador_2_bits multiplicador_2_bits_1 (
    .B2(B[1]), .A2(A[1]), .B1(B[0]), .A1(A[0]), .R4(multiplicador_2_bits_1_r4[0]),
    .R3(multiplicador_2_bits_1_r4[1]), .R2(multiplicador_2_bits_1_r4[2]), .R1(multiplicador_2_bits_1_r4[3]));
  _7_seg u_7_seg_1 (
    .A(out_4[3]), .B(out_4[2]), .C(out_4[1]), .D(out_4[0]), .A_2(n7_seg_1_a_2), .B_2(n7_seg_1_b_2),
    .C_2(n7_seg_1_c_2), .D_2(n7_seg_1_d_2), .E(n7_seg_1_e), .F(n7_seg_1_f), .G(n7_seg_1_g));
  _7_Segment_Display u_7_segment_display_1 (
    .g(n7_seg_1_g), .f(n7_seg_1_f), .a(n7_seg_1_a_2), .b(n7_seg_1_b_2), .e(n7_seg_1_e), .d(n7_seg_1_d_2),
    .c(n7_seg_1_c_2));  // open: dp
  LED led_1 (.in(out_4[4]));
endmodule

// -
module Subtrador_2_bits (
  input  A1,
  input  B1,
  input  A2,
  input  B2,
  output out_5,
  output out_6,
  output out_7
);

  wire and_1_out, and_2_out, and_3_out, and_4_out, and_5_out, and_6_out, not_1_out, not_2_out, not_3_out,
       not_4_out, or_2_out, xor_1_out, xor_3_out;

  not not_1 (not_1_out, A2);
  not not_2 (not_2_out, A2);
  xor xor_1 (xor_1_out, A2, B2);
  and and_1 (and_1_out, not_1_out, B2);
  and and_2 (and_2_out, not_2_out, or_2_out);
  and and_3 (and_3_out, B2, or_2_out);
  xor xor_2 (out_6, xor_1_out, or_2_out);
  or or_1 (out_5, and_1_out, and_2_out, and_3_out);
  not not_3 (not_3_out, A1);
  not not_4 (not_4_out, A1);
  xor xor_3 (xor_3_out, A1, B1);
  and and_4 (and_4_out, not_3_out, B1);
  and and_5 (and_5_out, not_4_out, 1'b0);
  and and_6 (and_6_out, B1, 1'b0);
  xor xor_4 (out_7, xor_3_out, 1'b0);
  or or_2 (or_2_out, and_4_out, and_5_out, and_6_out);
endmodule

// MUX
module MUX_4x1 (
  input  [4:0] Soma,
  input  [4:0] Subtra,
  input  [4:0] Multipli,
  input  [4:0] Divisao,
  input  BC1,
  input  BC2,
  output [4:0] out_7
);

  wire and_1_out, and_2_out, and_3_out, and_4_out, and_5_out, and_6_out, and_7_out, and_8_out, and_9_out,
       and_10_out, and_11_out, and_12_out, and_13_out, and_14_out, and_15_out, and_16_out, and_17_out,
       and_18_out, and_19_out, and_20_out, and_21_out, and_22_out, and_23_out, and_24_out, not_1_out,
       not_2_out, not_3_out, not_4_out;

  not not_1 (not_1_out, BC1);
  not not_2 (not_2_out, BC2);
  not not_3 (not_3_out, BC1);
  not not_4 (not_4_out, BC2);
  and and_1 (and_1_out, not_1_out, not_2_out);
  and and_2 (and_2_out, not_3_out, BC2);
  and and_3 (and_3_out, BC1, not_4_out);
  and and_4 (and_4_out, BC1, BC2);
  and and_5 (and_5_out, Soma[4], and_1_out);
  and and_6 (and_6_out, Subtra[4], and_2_out);
  and and_7 (and_7_out, Multipli[4], and_3_out);
  and and_8 (and_8_out, Divisao[4], and_4_out);
  and and_9 (and_9_out, Soma[0], and_1_out);
  and and_10 (and_10_out, Subtra[3], and_2_out);
  and and_11 (and_11_out, Multipli[3], and_3_out);
  and and_12 (and_12_out, Divisao[3], and_4_out);
  and and_13 (and_13_out, Soma[1], and_1_out);
  and and_14 (and_14_out, Subtra[2], and_2_out);
  and and_15 (and_15_out, Multipli[2], and_3_out);
  and and_16 (and_16_out, Divisao[2], and_4_out);
  and and_17 (and_17_out, Soma[2], and_1_out);
  and and_18 (and_18_out, Subtra[1], and_2_out);
  and and_19 (and_19_out, Multipli[1], and_3_out);
  and and_20 (and_20_out, Divisao[1], and_4_out);
  and and_21 (and_21_out, Soma[3], and_1_out);
  and and_22 (and_22_out, Subtra[0], and_2_out);
  and and_23 (and_23_out, Multipli[0], and_3_out);
  and and_24 (and_24_out, Divisao[0], and_4_out);
  or or_1 (out_7[4], and_5_out, and_6_out, and_7_out, and_8_out);
  or or_2 (out_7[0], and_9_out, and_10_out, and_11_out, and_12_out);
  or or_3 (out_7[1], and_13_out, and_14_out, and_15_out, and_16_out);
  or or_4 (out_7[2], and_17_out, and_18_out, and_19_out, and_20_out);
  or or_5 (out_7[3], and_21_out, and_22_out, and_23_out, and_24_out);
endmodule

// X
module Multiplicador_2_bits (
  input  B2,
  input  A2,
  input  B1,
  input  A1,
  output R4,
  output R3,
  output R2,
  output R1
);

  wire and_3_out, and_4_out, and_5_out, and_6_out, and_7_out, and_8_out, not_1_out, not_2_out, not_3_out,
       not_4_out, not_5_out, not_6_out;

  and and_1 (R4, A2, A1, B2, B1);
  not not_1 (not_1_out, A1);
  not not_2 (not_2_out, B1);
  not not_3 (not_3_out, A2);
  not not_4 (not_4_out, B1);
  not not_5 (not_5_out, A1);
  not not_6 (not_6_out, B2);
  and and_2 (R1, A1, B1);
  and and_3 (and_3_out, A2, not_1_out, B2);
  and and_4 (and_4_out, A2, B2, not_2_out);
  and and_5 (and_5_out, not_3_out, A1, B2);
  and and_6 (and_6_out, A1, B2, not_4_out);
  and and_7 (and_7_out, A2, not_5_out, B1);
  and and_8 (and_8_out, A2, not_6_out, B1);
  or or_1 (R3, and_3_out, and_4_out);
  or or_2 (R2, and_5_out, and_6_out, and_7_out, and_8_out);
endmodule

// %
module Divisor_2_bits (
  input  A2,
  input  A1,
  input  B2,
  input  B1,
  output Q1,
  output Q0,
  output R1,
  output R0,
  output E
);

  wire and_1_out, and_2_out, and_3_out, and_4_out, and_5_out, and_6_out, and_7_out, not_1_out, not_2_out,
       not_3_out, not_4_out, not_5_out, not_6_out, not_7_out, not_8_out, not_9_out;

  not not_1 (not_1_out, B2);
  and and_1 (and_1_out, A2, not_1_out, B1);
  not not_2 (not_2_out, A1);
  and and_2 (and_2_out, A2, not_2_out, B1);
  not not_3 (not_3_out, B2);
  and and_3 (and_3_out, A1, not_3_out, B1);
  and and_4 (and_4_out, A2, B2, not_4_out);
  not not_4 (not_4_out, B1);
  and and_5 (and_5_out, A2, A1, B2);
  not not_5 (not_5_out, A1);
  not not_6 (not_6_out, A2);
  and and_6 (and_6_out, not_6_out, A1, B2);
  and and_7 (and_7_out, A1, B2, not_7_out);
  not not_7 (not_7_out, B1);
  not not_8 (not_8_out, B2);
  and and_8 (E, not_8_out, not_9_out);
  not not_9 (not_9_out, B1);
  or or_1 (Q1, and_1_out, and_2_out);
  or or_2 (Q0, and_3_out, and_4_out, and_5_out);
  and and_9 (R1, A2, not_5_out, B2, B1);
  or or_3 (R0, and_6_out, and_7_out);
endmodule

module _7_seg (
  input  A,
  input  B,
  input  C,
  input  D,
  output A_2,
  output B_2,
  output C_2,
  output D_2,
  output E,
  output F,
  output G
);

  wire and_1_out, and_2_out, and_3_out, and_4_out, and_5_out, and_6_out, and_7_out, and_8_out, and_9_out,
       and_10_out, not_1_out, not_2_out, not_3_out, not_4_out, not_5_out, not_6_out, not_7_out, not_8_out,
       not_9_out, not_10_out, not_11_out, not_12_out, not_13_out, not_14_out, not_15_out, xnor_1_out,
       xnor_2_out, xor_1_out;

  not not_1 (not_1_out, B);
  not not_2 (not_2_out, C);
  not not_3 (not_3_out, B);
  not not_4 (not_4_out, D);
  not not_5 (not_5_out, B);
  not not_6 (not_6_out, D);
  not not_7 (not_7_out, C);
  not not_8 (not_8_out, B);
  not not_9 (not_9_out, D);
  not not_10 (not_10_out, D);
  not not_11 (not_11_out, C);
  not not_12 (not_12_out, D);
  not not_13 (not_13_out, C);
  not not_14 (not_14_out, D);
  not not_15 (not_15_out, D);
  xnor xnor_1 (xnor_1_out, B, D);
  xnor xnor_2 (xnor_2_out, C, D);
  or or_1 (C_2, B, not_2_out, D);
  and and_1 (and_1_out, not_3_out, not_4_out);
  and and_2 (and_2_out, not_5_out, C);
  and and_3 (and_3_out, C, not_6_out);
  and and_4 (and_4_out, B, not_7_out, D);
  and and_5 (and_5_out, not_8_out, not_9_out);
  and and_6 (and_6_out, C, not_10_out);
  and and_7 (and_7_out, not_11_out, not_12_out);
  and and_8 (and_8_out, B, not_13_out);
  and and_9 (and_9_out, B, not_14_out);
  xor xor_1 (xor_1_out, B, C);
  and and_10 (and_10_out, C, not_15_out);
  or or_2 (B_2, xnor_2_out, not_1_out);
  or or_3 (D_2, A, and_1_out, and_2_out, and_3_out, and_4_out);
  or or_4 (E, and_5_out, and_6_out);
  or or_5 (F, A, and_7_out, and_8_out, and_9_out);
  or or_6 (G, xor_1_out, A, and_10_out);
  or or_7 (A_2, xnor_1_out, C, A);
  _7_Segment_Display u_7_segment_display_1 (.g(G), .f(F), .a(A_2), .b(B_2), .e(E), .d(D_2), .c(C_2));  // open: dp
endmodule
