// Logisim project calculadora.circ as structural Verilog: 4 circuits, main circuit full adder
// +
module full_adder (
  input  A,
  input  B,
  input  Cin,
  output out_4,
  output out_5
);

  wire and_1_out, and_2_out, and_3_out, and_4_out, not_1_out, not_2_out, not_3_out, xor_1_out;

  not not_1 (not_1_out, A);
  not not_2 (not_2_out, B);
  not not_3 (not_3_out, Cin);
  xor xor_1 (xor_1_out, A, B);
  and and_1 (and_1_out, not_1_out, B, Cin);
  and and_2 (and_2_out, A, not_2_out, Cin);
  and and_3 (and_3_out, A, B, not_3_out);
  and and_4 (and_4_out, A, B, Cin);
  xor xor_2 (out_4, xor_1_out, Cin);
  or or_1 (out_5, and_1_out, and_2_out, and_3_out, and_4_out);
endmodule

module main (
);

  full_adder full_adder_1 ();  // open: A, B, Cin, out_4, out_5
  full_adder_2_bits full_adder_2_bits_1 ();  // open: A2, B2, out_6, A1, B1, Cin1, out_7, out_8, out_9
  full_subtractor full_subtractor_1 ();  // open: A, B, Bin, out_4, out_5
endmodule

// -
module full_subtractor (
  input  A,
  input  B,
  input  Bin,
  output out_4,
  output out_5
);

  wire and_1_out, and_2_out, and_3_out, not_1_out, xor_1_out;

  xor xor_1 (xor_1_out, A, B);
  not not_1 (not_1_out, A);
  and and_1 (and_1_out, not_1_out, B);
  and and_2 (and_2_out, not_1_out, Bin);
  and and_3 (and_3_out, B, Bin);
  xor xor_2 (out_4, xor_1_out, Bin);
  or or_1 (out_5, and_1_out, and_2_out, and_3_out);
endmodule

// FA 2 bits
module full_adder_2_bits (
  input  A1,
  input  B1,
  input  Cin1,
  input  A2,
  input  B2,
  output out_6,
  output out_7,
  output out_8,
  output out_9
);

  wire and_1_out, and_2_out, and_3_out, and_4_out, and_5_out, and_6_out, xor_1_out, xor_3_out;

  ExactlyOne xor_1 (.out(xor_1_out), .in0(A2), .in1(B2), .in2(out_6));
  buf and_1 (and_1_out, out_6);  // AND_Gate
  and and_2 (and_2_out, out_6, B2);
  and and_3 (and_3_out, B2, A2);
  or or_1 (out_7, and_1_out, and_2_out, and_3_out);
  xor xor_2 (out_8, xor_1_out, out_6);
  ExactlyOne xor_3 (.out(xor_3_out), .in0(A1), .in1(B1), .in2(Cin1));
  buf and_4 (and_4_out, Cin1);  // AND_Gate
  and and_5 (and_5_out, Cin1, B1);
  and and_6 (and_6_out, B1, A1);
  xor xor_4 (out_9, xor_3_out, Cin1);
  or or_2 (out_6, and_4_out, and_5_out, and_6_out);
endmodule
